# Fritzing sketch Rocco1 (saved by Fritzing 0.9.3b)
stripboards: 1

parts:
  J1 = Basic Servo
  J4 = male pin header, 3 pins [form="♂ (male)"]
  J6 = male pin header, 3 pins [form="♂ (male)"]
  Part1 = Arduino Mega 2560 (Rev3)
  Part2 = Bluetooth HC-05 Macho
  J7 = female pin header, 4 pins [form="♀ (female)"]
  J12 = male pin header, 3 pins [form="♂ (male)"]
  J13 = male pin header, 3 pins [form="♂ (male)"]
  J14 = male pin header, 3 pins [form="♂ (male)"]
  J15 = male pin header, 3 pins [form="♂ (male)"]
  J16 = male pin header, 3 pins [form="♂ (male)"]
  J17 = male pin header, 3 pins [form="♂ (male)"]
  J5 = male pin header, 3 pins [form="♂ (male)"]
  J27 = COMPUTER-PERIPHERAL-POWER [package=computer-peripheral-power-ra]
  S1 = SWITCH_SPDT [package=kps-1290]
  J10 = female pin header, 14 pins [form="♀ (female)"]
  J28 = female pin header, 2 pins [form="♀ (female)"]

nets:
  GND: J1.gnd, J4.pin3, J6.pin1, Part1.GND, Part2.GND, J7.pin2, J12.pin1, J13.pin1, J14.pin1, J15.pin1, J16.pin1, J17.pin1, J5.pin3, J28.pin1
  VCC: J1.vcc, J4.pin2, J6.pin2, J12.pin2, J13.pin2, J14.pin2, J15.pin2, J16.pin2, J17.pin2, J5.pin2, J27.5V
  N1: J1.pulse, Part1.D4_PWM, J5.pin1, J10.pin3
  N2: J4.pin1, Part1.D3_PWM, J10.pin4
  N3: J6.pin3, Part1.D2_PWM, J10.pin5
  N4: Part1.5V, S1.S, J28.pin2
  N5: Part1.D0_RX0, Part2.RXD, J7.pin4
  N6: Part1.D1_TX0, Part2.TXD, J7.pin3
  N7: Part2.VCC, J7.pin1, S1.O, S1.P
  N8: J27.GND, J10.pin1
