# Fritzing sketch Rocco_v2 (saved by Fritzing 0.9.3b)
stripboards: 3

parts:
  Part5 = Arduino Mega 2560 (Rev3)
  J45 = Basic Servo
  J46 = male pin header, 3 pins [form="♂ (male)"]
  J48 = male pin header, 3 pins [form="♂ (male)"]
  J50 = male pin header, 3 pins [form="♂ (male)"]
  J53 = male pin header, 3 pins [form="♂ (male)"]
  J55 = male pin header, 7 pins [form="♂ (male)"]
  J56 = male pin header, 3 pins [form="♂ (male)"]
  J57 = female pin header, 4 pins [form="♀ (female)"]
  J60 = male pin header, 8 pins [form="♂ (male)"]
  J61 = male pin header, 3 pins [form="♂ (male)"]
  J62 = male pin header, 3 pins [form="♂ (male)"]
  J63 = female pin header, 2 pins [form="♀ (female)"]
  J64 = male pin header, 3 pins [form="♂ (male)"]
  J65 = male pin header, 3 pins [form="♂ (male)"]
  J66 = male pin header, 3 pins [form="♂ (male)"]
  J67 = male pin header, 3 pins [form="♂ (male)"]
  J68 = male pin header, 3 pins [form="♂ (male)"]
  J69 = male pin header, 3 pins [form="♂ (male)"]
  R2 = Rotary Potentiometer (Large) [maximum_resistance=100kΩ package=THT]
  Part6 = Bluetooth HC-05 Macho
  S3 = SWITCH_SPDT [package=kps-1290]
  J71 = male pin header, 2 pins [form="♂ (male)"]
  J76 = male pin header, 9 pins [form="♂ (male)"]
  J77 = female pin header, 3 pins [form="♀ (female)"]
  J78 = female pin header, 2 pins [form="♀ (female)"]
  J79 = female pin header, 2 pins [form="♀ (female)"]
  J80 = female pin header, 2 pins [form="♀ (female)"]
  J82 = female pin header, 9 pins [form="♀ (female)"]
  J85 = male pin header, 3 pins [form="♂ (male)"]
  J86 = male pin header, 3 pins [form="♂ (male)"]
  J87 = male pin header, 3 pins [form="♂ (male)"]
  J88 = male pin header, 3 pins [form="♂ (male)"]
  J89 = male pin header, 3 pins [form="♂ (male)"]
  J90 = male pin header, 2 pins [form="♂ (male)"]
  J91 = male pin header, 2 pins [form="♂ (male)"]
  J81 = female pin header, 3 pins [form="♀ (female)"]
  J94 = male pin header, 2 pins [form="♂ (male)"]
  J95 = female pin header, 3 pins [form="♀ (female)"]
  J96 = male pin header, 2 pins [form="♂ (male)"]
  J97 = male pin header, 2 pins [form="♂ (male)"]
  J98 = female pin header, 3 pins [form="♀ (female)"]
  J99 = ATX24 Pin Power Supply Connector [package=atx24]

nets:
  N1: Part5.A2, R2.wiper, J77.pin2
  GND: Part5.GND, Part5.D1_TX0, J45.gnd, J46.pin1, J48.pin1, J50.pin1, J53.pin1, J55.pin1, J56.pin1, J57.pin2, J57.pin3, J60.pin2, J61.pin1, J62.pin3, J63.pin2, J64.pin1, J65.pin1, J66.pin3, J67.pin1, J68.pin1, J69.pin1, R2.leg1, Part6.TXD, Part6.GND, J71.pin2, J77.pin3, J78.pin2, J79.pin2, J80.pin2, J85.pin3, J86.pin3, J87.pin3, J88.pin3, J89.pin3, J90.pin2, J91.pin2, J94.pin1, J96.pin1, J97.pin1, J99.GND
  N2: Part5.D13_PWM, J55.pin2
  N3: Part5.D12_PWM, J55.pin3
  N4: Part5.D11_PWM, J55.pin4
  N5: Part5.D10_PWM, J55.pin5, J66.pin1
  N6: Part5.D9_PWM, J55.pin6, J86.pin1
  N7: Part5.D8_PWM, J55.pin7, J85.pin1
  N8: Part5.5V, J63.pin1, R2.leg2, S3.S, J77.pin1, J78.pin1, J79.pin1, J80.pin1
  VIN: Part5.VIN, J99.12V
  N9: Part5.D0_RX0, J57.pin1, J60.pin1, Part6.RXD
  N10: Part5.D2_PWM, J60.pin3, J89.pin1
  N11: Part5.D3_PWM, J60.pin4, J88.pin1
  N12: Part5.D4_PWM, J60.pin5, J87.pin1
  N13: Part5.D5_PWM, J60.pin6, J62.pin1
  N14: Part5.D6_PWM, J60.pin7, J67.pin3
  N15: Part5.D7_PWM, J60.pin8, J65.pin3
  N16: Part5.D37, J64.pin3, J76.pin9, J82.pin9, J98.pin3
  N17: Part5.D39, J46.pin3, J76.pin8, J82.pin8, J98.pin2
  N18: Part5.D41, J53.pin3, J76.pin7, J82.pin7, J98.pin1
  N19: Part5.D43, J50.pin3, J76.pin6, J82.pin6, J95.pin3
  N20: Part5.D45, J69.pin3, J76.pin5, J82.pin5, J95.pin2
  N21: Part5.D47, J56.pin3, J76.pin4, J82.pin4, J95.pin1
  N22: Part5.D49, J68.pin3, J76.pin3, J82.pin3, J81.pin3
  N23: Part5.D51, J48.pin3, J76.pin2, J82.pin2, J81.pin2
  N24: Part5.D53, J45.pulse, J61.pin3, J76.pin1, J82.pin1, J81.pin1
  VCC: J45.vcc, J46.pin2, J48.pin2, J50.pin2, J53.pin2, J56.pin2, J61.pin2, J62.pin2, J64.pin2, J65.pin2, J66.pin2, J67.pin2, J68.pin2, J69.pin2, J71.pin1, J85.pin2, J86.pin2, J87.pin2, J88.pin2, J89.pin2, J90.pin1, J91.pin1, J94.pin2, J96.pin2, J97.pin2, J99.5V
  N25: J57.pin4, Part6.VCC, S3.O, S3.P
