# Fritzing sketch Rocco_v5 (saved by Fritzing 0.9.3b)
stripboards: 3

parts:
  Part5 = Arduino Mega 2560 (Rev3)
  J45 = Basic Servo
  J46 = male pin header, 3 pins [form="♂ (male)"]
  J48 = male pin header, 3 pins [form="♂ (male)"]
  J50 = male pin header, 3 pins [form="♂ (male)"]
  J53 = male pin header, 3 pins [form="♂ (male)"]
  J56 = male pin header, 3 pins [form="♂ (male)"]
  J57 = female pin header, 4 pins [form="♀ (female)"]
  J60 = male pin header, 8 pins [form="♂ (male)"]
  J61 = male pin header, 3 pins [form="♂ (male)"]
  J62 = male pin header, 3 pins [form="♂ (male)"]
  J63 = female pin header, 2 pins [form="♀ (female)"]
  J64 = male pin header, 3 pins [form="♂ (male)"]
  J65 = male pin header, 3 pins [form="♂ (male)"]
  J66 = male pin header, 3 pins [form="♂ (male)"]
  J67 = male pin header, 3 pins [form="♂ (male)"]
  J68 = male pin header, 3 pins [form="♂ (male)"]
  J69 = male pin header, 3 pins [form="♂ (male)"]
  Part6 = Bluetooth HC-05 Macho
  S3 = SWITCH_SPDT [package=kps-1290]
  J76 = male pin header, 9 pins [form="♂ (male)"]
  J79 = female pin header, 2 pins [form="♀ (female)"]
  J80 = female pin header, 2 pins [form="♀ (female)"]
  J82 = female pin header, 9 pins [form="♀ (female)"]
  J85 = male pin header, 3 pins [form="♂ (male)"]
  J86 = male pin header, 3 pins [form="♂ (male)"]
  J87 = male pin header, 3 pins [form="♂ (male)"]
  J88 = male pin header, 3 pins [form="♂ (male)"]
  J89 = male pin header, 3 pins [form="♂ (male)"]
  J81 = female pin header, 3 pins [form="♀ (female)"]
  J95 = female pin header, 3 pins [form="♀ (female)"]
  J98 = female pin header, 3 pins [form="♀ (female)"]
  J100 = Screw terminal - 2 pins [package=THT]
  J101 = Screw terminal - 2 pins [package=THT]
  J102 = Screw terminal - 2 pins [package=THT]
  J103 = Screw terminal - 2 pins [package=THT]
  J104 = Screw terminal - 2 pins [package=THT]
  J105 = Screw terminal - 2 pins [package=THT]
  J99 = ATX24 Pin Power Supply Connector [package=atx24]
  J106 = male pin header, 2 pins [form="♂ (male)"]
  J107 = male pin header, 3 pins [form="♂ (male)"]

nets:
  GND: Part5.GND, J45.gnd, J46.pin1, J48.pin1, J50.pin1, J53.pin1, J56.pin1, J61.pin1, J62.pin3, J64.pin1, J65.pin1, J66.pin3, J67.pin1, J68.pin1, J69.pin1, J85.pin3, J86.pin3, J87.pin3, J88.pin3, J89.pin3, J100.pin1, J101.pin2, J102.pin1, J103.pin1, J104.pin2, J105.pin2, J99.GND, J106.pin1
  N1: Part5.D13_PWM, J106.pin2
  N2: Part5.D10_PWM, J66.pin1, J107.pin1
  N3: Part5.D9_PWM, J86.pin1, J107.pin2
  N4: Part5.D8_PWM, J85.pin1, J107.pin3
  VIN: Part5.VIN, J99.12V
  N5: Part5.D0_RX0, J57.pin1, J60.pin1, Part6.RXD
  N6: Part5.D1_TX0, J57.pin2, J57.pin3, J60.pin2, J63.pin2, Part6.TXD, Part6.GND, J79.pin2, J80.pin2
  N7: Part5.D2_PWM, J60.pin3, J89.pin1
  N8: Part5.D3_PWM, J60.pin4, J88.pin1
  N9: Part5.D4_PWM, J60.pin5, J87.pin1
  N10: Part5.D5_PWM, J60.pin6, J62.pin1
  N11: Part5.D6_PWM, J60.pin7, J67.pin3
  N12: Part5.D7_PWM, J60.pin8, J65.pin3
  N13: Part5.D37, J76.pin9
  N14: Part5.D39, J76.pin8
  N15: Part5.D41, J76.pin7
  N16: Part5.D43, J76.pin6
  N17: Part5.D45, J76.pin5
  N18: Part5.D47, J76.pin4
  N19: Part5.D49, J76.pin3
  N20: Part5.D51, J76.pin2
  N21: Part5.D53, J76.pin1
  VCC: J45.vcc, J46.pin2, J48.pin2, J50.pin2, J53.pin2, J56.pin2, J61.pin2, J62.pin2, J64.pin2, J65.pin2, J66.pin2, J67.pin2, J68.pin2, J69.pin2, J85.pin2, J86.pin2, J101.pin1, J102.pin2, J103.pin2, J104.pin1, J105.pin1, J99.5V
  N22: J45.pulse, J61.pin3, J82.pin1, J81.pin1
  N23: J46.pin3, J82.pin8, J98.pin2
  N24: J48.pin3, J82.pin2, J81.pin2
  N25: J50.pin3, J82.pin4, J95.pin1
  N26: J53.pin3, J82.pin7, J98.pin1
  N27: J56.pin3, J82.pin5, J95.pin2
  N28: J57.pin4, Part6.VCC, S3.O, S3.P
  N29: J63.pin1, S3.S, J79.pin1, J80.pin1
  N30: J64.pin3, J82.pin9, J98.pin3
  N31: J68.pin3, J82.pin3, J81.pin3
  N32: J69.pin3, J82.pin6, J95.pin3
  N33: J87.pin2, J88.pin2, J89.pin2, J100.pin2, J99.CUSTOM_5V

custom parts:
  Screw terminal - 2 pins: Screw terminal with 2 pins
