# Fritzing sketch Rocco_v8 (saved by Fritzing 0.9.3b)
stripboards: 4

parts:
  Part5 = Arduino Mega 2560 (Rev3)
  J45 = Basic Servo
  J46 = male pin header, 3 pins [form="♂ (male)"]
  J48 = male pin header, 3 pins [form="♂ (male)"]
  J50 = male pin header, 3 pins [form="♂ (male)"]
  J53 = male pin header, 3 pins [form="♂ (male)"]
  J56 = male pin header, 3 pins [form="♂ (male)"]
  J57 = female pin header, 4 pins [form="♀ (female)"]  # not connected
  J61 = male pin header, 3 pins [form="♂ (male)"]
  J62 = male pin header, 3 pins [form="♂ (male)"]
  J63 = female pin header, 2 pins [form="♀ (female)"]
  J64 = male pin header, 3 pins [form="♂ (male)"]
  J65 = male pin header, 3 pins [form="♂ (male)"]
  J66 = male pin header, 3 pins [form="♂ (male)"]
  J67 = male pin header, 3 pins [form="♂ (male)"]
  J68 = male pin header, 3 pins [form="♂ (male)"]
  J69 = male pin header, 3 pins [form="♂ (male)"]
  Part6 = Bluetooth HC-05 Macho  # not connected
  S3 = SWITCH_SPDT [package=kps-1290]
  J80 = female pin header, 2 pins [form="♀ (female)"]  # not connected
  J85 = male pin header, 3 pins [form="♂ (male)"]
  J86 = male pin header, 3 pins [form="♂ (male)"]
  J87 = male pin header, 3 pins [form="♂ (male)"]  # not connected
  J88 = male pin header, 3 pins [form="♂ (male)"]  # not connected
  J89 = male pin header, 3 pins [form="♂ (male)"]
  J99 = ATX24 Pin Power Supply Connector [package=atx24]
  C3 = Capacitor Polarized [package=cpol-radial-1000uf-25v]  # not connected
  JP1 = Screw Terminal [package=screwterminal-3.5mm-2_lock]  # not connected
  JP2 = Screw Terminal [package=screwterminal-3.5mm-2_lock]  # not connected
  JP3 = Screw Terminal [package=screwterminal-3.5mm-2_lock]  # not connected
  JP4 = Screw Terminal [package=screwterminal-3.5mm-2_lock]
  JP5 = Screw Terminal [package=screwterminal-3.5mm-2_lock]
  JP6 = Screw Terminal [package=screwterminal-3.5mm-2_lock]
  C6 = Capacitor Polarized [package=cpol-radial-1000uf-25v]
  C7 = Capacitor Polarized [package=cpol-radial-1000uf-25v]
  C8 = Capacitor Polarized [package=cpol-radial-1000uf-25v]  # not connected
  C9 = Capacitor Polarized [package=cpol-radial-1000uf-25v]  # not connected
  C10 = Capacitor Polarized [package=cpol-radial-1000uf-25v]  # not connected
  Part7 = HY-SRF05 Ultrasonic Rangefinder  # not connected
  J108 = female pin header, 3 pins [form="♀ (female)"]
  J109 = female pin header, 3 pins [form="♀ (female)"]
  J110 = female pin header, 3 pins [form="♀ (female)"]
  J111 = female pin header, 3 pins [form="♀ (female)"]  # not connected
  J112 = female pin header, 3 pins [form="♀ (female)"]
  J113 = female pin header, 3 pins [form="♀ (female)"]
  J107 = male pin header, 5 pins [form="♂ (male)"]  # not connected
  J114 = female pin header, 2 pins [form="♀ (female)"]
  C15 = Ceramic Capacitor [capacitance=100nF package="200 mil [THT, multilayer]"]
  C16 = Ceramic Capacitor [capacitance=100nF package="200 mil [THT, multilayer]"]
  C17 = Ceramic Capacitor [capacitance=100nF package="200 mil [THT, multilayer]"]
  C18 = Ceramic Capacitor [capacitance=100nF package="200 mil [THT, multilayer]"]
  C19 = Ceramic Capacitor [capacitance=100nF package="200 mil [THT, multilayer]"]
  C20 = Ceramic Capacitor [capacitance=100nF package="200 mil [THT, multilayer]"]
  C21 = Ceramic Capacitor [capacitance=100nF package="200 mil [THT, multilayer]"]
  C22 = Ceramic Capacitor [capacitance=100nF package="200 mil [THT, multilayer]"]
  C23 = Ceramic Capacitor [capacitance=100nF package="200 mil [THT, multilayer]"]
  C24 = Ceramic Capacitor [capacitance=100nF package="200 mil [THT, multilayer]"]
  C25 = Ceramic Capacitor [capacitance=100nF package="200 mil [THT, multilayer]"]
  C26 = Ceramic Capacitor [capacitance=100nF package="200 mil [THT, multilayer]"]
  C27 = Ceramic Capacitor [capacitance=100nF package="200 mil [THT, multilayer]"]
  C28 = Ceramic Capacitor [capacitance=100nF package="200 mil [THT, multilayer]"]
  C29 = Ceramic Capacitor [capacitance=100nF package="200 mil [THT, multilayer]"]
  C30 = Ceramic Capacitor [capacitance=100nF package="200 mil [THT, multilayer]"]
  C31 = Ceramic Capacitor [capacitance=100nF package="200 mil [THT, multilayer]"]
  C32 = Ceramic Capacitor [capacitance=100nF package="200 mil [THT, multilayer]"]
  C34 = Ceramic Capacitor [package="1206 [SMD, multilayer]"]
  C35 = Ceramic Capacitor [package="1206 [SMD, multilayer]"]
  C36 = Ceramic Capacitor [package="1206 [SMD, multilayer]"]
  C37 = Ceramic Capacitor [package="1206 [SMD, multilayer]"]
  C38 = Ceramic Capacitor [package="1206 [SMD, multilayer]"]
  C39 = Ceramic Capacitor [package="1206 [SMD, multilayer]"]
  R8 = Resistor [tolerance=±5% resistance=10k package="0603 [SMD]"]
  R13 = Resistor [tolerance=±5% resistance=10k package="0603 [SMD]"]
  R11 = Resistor [tolerance=±5% resistance=10k package="0603 [SMD]"]
  R16 = Resistor [tolerance=±5% resistance=10k package="0603 [SMD]"]
  R14 = Resistor [tolerance=±5% resistance=10k package="0603 [SMD]"]
  R6 = Resistor [tolerance=±5% resistance=10k package="0603 [SMD]"]
  R4 = Resistor [tolerance=±5% resistance=10k package="0603 [SMD]"]
  R9 = Resistor [tolerance=±5% resistance=10k package="0603 [SMD]"]
  R7 = Resistor [tolerance=±5% resistance=10k package="0603 [SMD]"]
  R2 = Resistor [tolerance=±5% resistance=10k package="0603 [SMD]"]
  R5 = Resistor [tolerance=±5% resistance=10k package="0603 [SMD]"]
  R12 = Resistor [tolerance=±5% resistance=10k package="0603 [SMD]"]
  R17 = Resistor [tolerance=±5% resistance=10k package="0603 [SMD]"]
  R10 = Resistor [tolerance=±5% resistance=10k package="0603 [SMD]"]
  R15 = Resistor [tolerance=±5% resistance=10k package="0603 [SMD]"]
  R18 = Resistor [tolerance=±5% resistance=10k package="0603 [SMD]"]
  J116 = male pin header, 2 pins [form="♂ (male)"]
  R19 = Resistor [tolerance=±5% resistance=10k package="0603 [SMD]"]
  R20 = Resistor [tolerance=±5% resistance=10k package="0603 [SMD]"]
  J119 = female pin header, 18 pins [form="♀ (female)"]
  J120 = male pin header, 2 pins [form="♂ (male)"]
  J115 = male pin header, 15 pins [form="♂ (male)"]
  J121 = male pin header, 1 pin [form="♂ (male)"]

nets:
  N1: Part5.5V, S3.P, J114.pin2
  GND: Part5.GND, J99.GND, JP4.2, JP5.2, JP6.2, J114.pin1
  VIN: Part5.VIN, J99.12V
  N2: Part5.D0_RX0, J63.pin2
  N3: Part5.D1_TX0, J63.pin1
  N4: J45.gnd, J66.pin1
  N5: J45.vcc, J66.pin2
  N6: J45.pulse, J66.pin3
  N7: J46.pin1, J64.pin1, J65.pin3, C6.-
  N8: J46.pin2, J64.pin2, J65.pin2, C6.+
  N9: J46.pin3, J109.pin1
  N10: J48.pin1, J61.pin1, J68.pin1
  N11: J48.pin2, J61.pin2, J68.pin2
  N12: J48.pin3, J113.pin2
  N13: J50.pin1, J56.pin1, J69.pin1
  N14: J50.pin2, J56.pin2, J69.pin2
  N15: J50.pin3, J112.pin1
  N16: J53.pin1, J62.pin1, J67.pin3, C7.-
  N17: J53.pin2, J62.pin2, J67.pin2, C7.+
  N18: J53.pin3, J110.pin1
  N19: J56.pin3, J112.pin2
  N20: J61.pin3, J113.pin1
  N21: J62.pin3, J110.pin2
  N22: J64.pin3, J109.pin3
  N23: J65.pin1, J109.pin2
  N24: J67.pin1, J110.pin3
  N25: J68.pin3, J113.pin3
  N26: J69.pin3, J112.pin3
  N27: J85.pin1, J86.pin1, J89.pin1
  N28: J85.pin2, J86.pin2, J89.pin2
  N29: J85.pin3, J108.pin2
  N30: J86.pin3, J108.pin1
  N31: J89.pin3, J108.pin3
  N32: J99.5V, JP4.1, JP5.1, JP6.1
  N33: C15.0, C16.0, C17.0, C34.0
  N34: C18.0, C19.0, C20.0, C37.0
  N35: C21.0, C22.0, C26.0, C35.0
  N36: C23.0, C24.0, C25.0, C38.0
  N37: C27.0, C28.0, C32.0, C36.0
  N38: C29.0, C30.0, C31.0, C39.0
  N39: R8.Pin_0, R13.Pin_0, R11.Pin_0, R16.Pin_0, R14.Pin_0, R6.Pin_0, R4.Pin_0, R9.Pin_0, R7.Pin_0, R2.Pin_0, R5.Pin_0, R12.Pin_0, R17.Pin_0, R10.Pin_0, R15.Pin_0, R18.Pin_0, R19.Pin_0, R20.Pin_0, J121.pin1
  N40: R8.Pin_1, J119.pin13, J115.pin14
  N41: R13.Pin_1, J119.pin10, J115.pin11
  N42: R11.Pin_1, J119.pin4, J115.pin5
  N43: R16.Pin_1, J119.pin1, J115.pin2
  N44: R14.Pin_1, J119.pin3, J115.pin4
  N45: R6.Pin_1, J116.pin1, J119.pin16, J120.pin1
  N46: R4.Pin_1, J116.pin2, J119.pin15, J120.pin2
  N47: R9.Pin_1, J119.pin14, J115.pin15
  N48: R7.Pin_1, J119.pin5, J115.pin6
  N49: R2.Pin_1, J119.pin7, J115.pin8
  N50: R5.Pin_1, J119.pin6, J115.pin7
  N51: R12.Pin_1, J119.pin12, J115.pin13
  N52: R17.Pin_1, J119.pin8, J115.pin9
  N53: R10.Pin_1, J119.pin11, J115.pin12
  N54: R15.Pin_1, J119.pin9, J115.pin10
  N55: R18.Pin_1, J119.pin2, J115.pin3
  N56: R19.Pin_1, J119.pin18
  N57: R20.Pin_1, J119.pin17

notes:
  PCB2: Resistors and 2 signal jumper wires go on back
  PCB1: Bottom -
  6 x .33uF at board edges, ...
  PCB1: Top -

custom parts:
  Screw Terminal: Screw terminal, takes up three holes.
  Ceramic Capacitor: 0.33 uF multilayered Ceramic Capacitor
